# Fritzing sketch various (saved by Fritzing 0.9.0b)
breadboards: 1

parts:
  Axoloti1 = Axoloti Core Beta [package=beta]
  R1 = Resistor [tolerance=±5% resistance=220 package=THT]
  LED1 = LED - 5mm [color="Red (633nm)" package="5 mm [THT]"]
  Part1 = Triple Axis Accelerometer Breakout - ADXL335
  R2 = Rotary Potentiometer (Small) [maximum_resistance=100kΩ package=THT]
  S1 = Pushbutton [package="[THT]"]
  R3 = Photocell (LDR) [package=THT]
  R4 = Resistor [tolerance=±5% resistance=100k package=THT]
  J1 = Basic Servo
  J2 = Basic Force Sensing Resistor (FSR) [package=THT]
  R5 = Basic Flex Resistor
  J3 = Infrared Proximity Sensor
  R6 = Resistor [tolerance=±5% resistance=22k package=THT]
  R8 = Resistor [tolerance=±5% resistance=22k package=THT]

nets:
  VCC: Axoloti1.+5V, J1.vcc, J3.Vcc
  N1: Axoloti1.PB9, R1.Pin_0
  N2: Axoloti1.PB8, J1.pulse
  GND: Axoloti1.GND#3, LED1.cathode, R2.leg1, R3.pin_0, J1.gnd, J2.pin_1, R5.Pin_2, J3.GND
  N3: Axoloti1.PC0, J3.Vout
  N4: Axoloti1.VDD#10, R2.leg2, S1.Pin_3, S1.Pin_4, R4.Pin_1, R6.Pin_1, R8.Pin_1
  N5: Axoloti1.PA0, S1.Pin_1, S1.Pin_2
  N6: Axoloti1.PA2, R3.pin_1, R4.Pin_0
  N7: Axoloti1.PA7, J2.pin_0, R6.Pin_0
  N8: Axoloti1.VDD#20, Part1.VCC
  N9: Axoloti1.GND#21, Part1.GND
  N10: Axoloti1.PB0, Part1.XOUT
  N11: Axoloti1.PC5, Part1.YOUT
  N12: Axoloti1.PC4, Part1.ZOUT
  N13: Axoloti1.PB1, R2.wiper
  N14: Axoloti1.PC7, R5.pin_1, R8.Pin_0
  N15: R1.Pin_1, LED1.anode

notes:
  use gpio/in/analog for accelerometer
  use gpio/in/analog for ligtsensor
  use gpio/in/digital with pulldown selected for button
  use gpio/in/analog...
  use gpio/out/pwm t4 servo for servos
  use gpio/out/digital for LED
